# Fritzing sketch orphybot_testbed (saved by Fritzing 0.9.3b)
breadboards: 1

parts:
  Part1 = Arduino Uno (Rev3) - ICSP
  LED2 = LEDs [package=led10mm]
  LED3 = LEDs [package=led10mm]
  R2 = Resistor [tolerance=±5% resistance=220 package="0805 [SMD]"]
  R3 = Resistor [tolerance=±5% resistance=220 package="0805 [SMD]"]
  J2 = Screw terminal - 2 pins [package=THT]
  J3 = Screw terminal - 2 pins [package=THT]  # not connected
  J4 = Screw terminal - 2 pins [package=THT]
  J5 = Screw terminal - 2 pins [package=THT]
  J6 = Screw terminal - 2 pins [package=THT]
  J7 = Screw terminal - 2 pins [package=THT]
  L298N1 = L298N DC motor driver
  L298N2 = L298N DC motor driver
  M1 = DC Motor
  M2 = DC Motor
  M4 = DC Motor
  M5 = DC Motor
  HC-1 = HC-12 Module
  Antenna1 = HC-12 Antenna
  VCC1 = Battery

nets:
  N1: Part1.ICSP_MISO, Part1.D12/MISO, L298N2.IN4
  N2: Part1.ICSP_MOSI, Part1.D11_PWM/MOSI, L298N2.ENB
  GND: Part1.GND, LED2.A, LED3.A, J4.pin1, J5.pin1, J6.pin1, J7.pin1, L298N1.GND, L298N2.GND, HC-1.GND, VCC1.-
  N3: Part1.D8, L298N2.IN1
  N4: Part1.D9_PWM, L298N2.ENA
  N5: Part1.D10_PWM/SS, L298N1.ENB
  N6: Part1.D13/SCK, L298N2.IN3
  N7: Part1.D0/RX, HC-1.TXD
  N8: Part1.D1/TX, HC-1.RXD
  N9: Part1.D2, L298N1.IN1
  N10: Part1.D3_PWM, L298N1.ENA
  N11: Part1.D4, L298N1.IN2
  N12: Part1.D5_PWM, L298N1.IN3
  N13: Part1.D6_PWM, L298N1.IN4
  N14: Part1.D7, L298N2.IN2
  5V: Part1.5V, R2.Pin_1, R3.Pin_1, J2.pin1, J2.pin2, L298N1.5V, HC-1.VCC
  N15: LED2.C, R3.Pin_0
  N16: LED3.C, R2.Pin_0
  12V: J4.pin2, J5.pin2, J6.pin2, J7.pin2, L298N1.12V, L298N2.12V, VCC1.+
  N17: L298N1.OUT1, M5.pin_2
  N18: L298N1.OUT2, M5.pin_1
  N19: L298N1.OUT3, M4.pin_2
  N20: L298N1.OUT4, M4.pin_1
  N21: L298N2.OUT1, M1.pin_2
  N22: L298N2.OUT2, M1.pin_1
  N23: L298N2.OUT3, M2.pin_2
  N24: L298N2.OUT4, M2.pin_1
  N25: HC-1.ANT, Antenna1.ANT

custom parts:
  L298N DC motor driver: 2x DC motor driver with 78M05 positive voltage regulator (7..35 V) L298N: max 46 V, 2 A Set 5 V Enable jumper to enable 5 V regultor (needed for the L298N) and +5 V output at screw terminal or supply external +5 V at screw terminal Set ENA and/or ENB to +5 V to enable motor permanently or supply ENA and/or ENB with PWM signal IN1 and IN2 set rotation directory for motor A (OUT1/OUT2) IN2 and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
  HC-12 Module: HC-12 433Mhz Module
  HC-12 Antenna: Antenna for HC-12 433Mhz Module
  Battery: Your standard 2x 18650 battery pack (7,4 Volts)
